# Fritzing sketch energy-node (saved by Fritzing 1.0.3b)
breadboards: 1

parts:
  SCT-013_2 = Microphone
  SCT-013_1 = Microphone
  R1 = Resistor [tolerance=±5% resistance=120 package="2512 [SMD]"]
  R3 = Resistor [tolerance=±5% resistance=120 package="2512 [SMD]"]
  R5 = Resistor [tolerance=±5% resistance=470k package="2512 [SMD]"]
  R6 = Resistor [tolerance=±5% resistance=470k package="2512 [SMD]"]
  R7 = Resistor [tolerance=±5% resistance=470k package="2512 [SMD]"]
  R8 = Resistor [tolerance=±5% resistance=470k package="2512 [SMD]"]
  C2 = Electrolytic Capacitor [capacitance=10µF voltage=35V package="100 mil [THT, electrolytic]"]
  C3 = Electrolytic Capacitor [capacitance=10µF voltage=35V package="100 mil [THT, electrolytic]"]
  Arduino_Leonardo = Arduino Leonardo (Rev3b)
  M1 = DOIT Esp32 DevKit v1 (30 pins long, 11 pins width) [part_number=ESP32S-PIN30]

nets:
  N1: SCT-013_2.pin1, R1.Pin_1, R5.Pin_0, R7.Pin_1, C2.+
  N2: SCT-013_2.pin2, R1.Pin_0, Arduino_Leonardo.A1
  N3: SCT-013_1.pin1, R3.Pin_1, R6.Pin_0, R8.Pin_1, C3.+
  N4: SCT-013_1.pin2, R3.Pin_0, Arduino_Leonardo.A0
  N5: R5.Pin_1, R6.Pin_1
  GND: R7.Pin_0, R8.Pin_0, C2.-, C3.-, Arduino_Leonardo.GND, M1.GND
  N6: Arduino_Leonardo.D11_PWM, M1.TX2
  N7: Arduino_Leonardo.D12/A11, M1.RX2

custom parts:
  DOIT Esp32 DevKit v1 (30 pins long, 11 pins width): The DOIT Esp32 DevKit v1 is one of the development board created by DOIT to evaluate the ESP-WROOM-32 module. It is based on the ESP32 microcontroller that boasts Wifi, Bluetooth, Ethernet and Low Power support all in a single chip. (vanepp) made breadboard work, adjusted pin numbering and labels and reduced size of schematic and cleaned up pcb. This chip is 30pins long (2 x15) and 11 pins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
